# Fritzing sketch DHT11-RPi (saved by Fritzing 0.9.3b)
breadboards: 1

parts:
  Componente1 = Adafruit T-Cobbler Plus [part_number="Adafruit #1989 and #2028"]
  Mod1 = KY-015 Temperature & Humidity Sensor Module [package="Breakout board"]

nets:
  +3.3V: Componente1.+3.3V, Mod1.Vin
  N1: Componente1.GPIO4, Mod1.S
  N2: Componente1.GND, Mod1.-

custom parts:
  Adafruit T-Cobbler Plus: The Raspberry Pi has landed on the Maker World like a 40-GPIO pinned, quad-USB ported, credit card sized bomb of DIY joy. And while you can use most of our great Model B accessories by hooking up our downgrade cable, its probably a good time to upgrade your set up and accessorize using all of the 40 pins. That's why we now carry the Assembled Adafruit Pi T-Cobbler Plus - Breakout + Cable for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
  KY-015 Temperature & Humidity Sensor Module: KY-015 temperature and humidity sensor module, provides a low-latency serial interface to measure humidity and temperature.
