# Fritzing sketch HCSR04-RPi (saved by Fritzing 0.9.3b)
breadboards: 1

parts:
  Componente1 = Adafruit T-Cobbler Plus [part_number="Adafruit #1989 and #2028"]
  Componente2 = SRF05 Ultrasonic Rangefinder
  R1 = Resistor [tolerance=±5% resistance=1k package="1206 [SMD]"]
  R2 = Resistor [tolerance=±5% resistance=1k package="1206 [SMD]"]
  R3 = Resistor [tolerance=±5% resistance=1k package="1206 [SMD]"]

nets:
  GND: Componente1.GND, Componente2.GND, R3.Pin_1
  +5V: Componente1.+5V, Componente2.VCC
  N1: Componente1.GPIO23, Componente2.Trig
  N2: Componente1.GPIO24, R2.Pin_1, R3.Pin_0
  N3: Componente2.Echo, R1.Pin_0
  N4: R1.Pin_1, R2.Pin_0

custom parts:
  Adafruit T-Cobbler Plus: The Raspberry Pi has landed on the Maker World like a 40-GPIO pinned, quad-USB ported, credit card sized bomb of DIY joy. And while you can use most of our great Model B accessories by hooking up our downgrade cable, its probably a good time to upgrade your set up and accessorize using all of the 40 pins. That's why we now carry the Assembled Adafruit Pi T-Cobbler Plus - Breakout + Cable for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
