# Fritzing sketch higrometro (saved by Fritzing 0.9.3b)
breadboards: 1

parts:
  Componente1 = Adafruit T-Cobbler Plus [part_number="Adafruit #1989 and #2028"]
  Componente2 = FC-28 Soil Hygrometer Module
  LED1 = LED - 5mm [color="Red (633nm)" package="5 mm [THT]"]
  LED2 = LED - 5mm [color="Green (555nm)" package="5 mm [THT]"]
  Componente3 = FC-28 Soil Hygrometer Module - Probe

nets:
  GND: Componente1.GND, Componente2.GND, LED1.cathode, LED2.cathode
  N1: Componente1.GPIO22, LED2.anode
  N2: Componente1.+3.3V_2, LED1.anode
  +5V: Componente1.+5V, Componente2.VCC
  N3: Componente1.GPIO23, Componente2.DO
  N4: Componente2.POS, Componente3.POS
  N5: Componente2.NEG, Componente3.NEG

custom parts:
  Adafruit T-Cobbler Plus: The Raspberry Pi has landed on the Maker World like a 40-GPIO pinned, quad-USB ported, credit card sized bomb of DIY joy. And while you can use most of our great Model B accessories by hooking up our downgrade cable, its probably a good time to upgrade your set up and accessorize using all of the 40 pins. That's why we now carry the Assembled Adafruit Pi T-Cobbler Plus - Breakout + Cable for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
  FC-28 Soil Hygrometer Module: The FC-28 is a soil hygrometer module that uses the Texas Instruments LM393 comparator chip to provide an analog measurement of soil humidity. The digital output is high when soil moisture is over a certain threshold, as determined by adjusting the potentiometer.
  FC-28 Soil Hygrometer Module - Probe: The FC-28 is a soil hygrometer module that uses the Texas Instruments LM393 comparator chip to provide an analog measurement of soil humidity.
